# Fritzing sketch atmega328-rs485-modbus-data-logger-NG (saved by Fritzing 0.9.3b)

parts:
  Part1 = Arduino Uno (Rev3)
  RS485_module1 = RS485 Module (MAX3485)
  TRM1 = Terminal 2pin

nets:
  N1: Part1.D10_PWM/SS, RS485_module1.RO
  N2: Part1.D11_PWM/MOSI, RS485_module1.DI
  GND: Part1.GND, RS485_module1.GND
  N3: Part1.D4, RS485_module1.RE, RS485_module1.DE
  5V: Part1.5V, RS485_module1.VCC
  N4: RS485_module1.A, TRM1.pin_1
  N5: RS485_module1.B, TRM1.pin_2

custom parts:
  RS485 Module (MAX3485): Commercially available RS485 to RS232 TTL Module
  Terminal 2pin: 2-pin Terminal Block
